# Fritzing sketch BTcar (saved by Fritzing 0.9.2b)
breadboards: 1

parts:
  Part1 = Arduino Mega 2560 (Rev3)
  Part2 = Bluetooth Mate Silver
  U1 = L298 [package=multiwatt15_6400bgheatsink]
  M1 = DC Motor
  M2 = DC Motor
  U2 = SPM0204UD5 [package=spm0204ud5]  # not connected
  VCC1 = 4 x AAA Battery Mount

nets:
  GND: Part1.GND, Part2.GND, VCC1.+
  N1: Part1.D12_PWM, Part2.TX_5V
  N2: Part1.D11_PWM, Part2.RX_5V
  N3: Part1.IOREF, Part2.VCC
  N4: Part1.D2_PWM, U1.IN1
  N5: Part1.D3_PWM, U1.IN2
  N6: U1.OUT1, M1.pin_1
  N7: U1.OUT2, M1.pin_2
  N8: U1.VS, VCC1.-
  N9: U1.OUT4, M2.pin_2
